// Logisim project Multiplexer_Agnes_Duru.circ as structural Verilog: 1 circuit, main circuit main
module main (
  input  D
);

  wire clock_1_out, Jb, Jc, not_1_out, nQa, nQb, nQc, Qa, Qb, Qc, undriven, undriven_2;

  not not_1 (not_1_out, D);
  Multiplexer #(.select(3), .enable("false")) multiplexer_1 (
    .in0(D), .in1(not_1_out), .in2(D), .in3(not_1_out), .in4(D), .in5(not_1_out), .in6(D), .in7(not_1_out),
    .out(Jb), .sel({Qc, Qb, Qa}));
  Multiplexer #(.select(3), .enable("false")) multiplexer_2 (
    .in0(D), .in1(1'b0), .in2(1'b0), .in3(not_1_out), .in4(D), .in5(1'b0), .in6(1'b0), .in7(not_1_out),
    .out(Jc), .sel({Qc, Qb, Qa}));
  Clock clock_1 (.out(clock_1_out));
  J_K_Flip_Flop j_k_ff_1 (.J(Jc), .K(Jc), .clk(clock_1_out), .Q(Qc), .Qn(nQc), .reset(undriven));  // open: preset
  J_K_Flip_Flop j_k_ff_2 (.J(Jb), .K(Jb), .clk(clock_1_out), .Q(Qb), .Qn(nQb), .preset(undriven), .reset(undriven_2));
  J_K_Flip_Flop j_k_ff_3 (.J(1'b1), .K(1'b1), .clk(clock_1_out), .Q(Qa), .Qn(nQa), .preset(undriven_2));  // open: reset
  Hex_Digit_Display hex_digit_display_1 (.value({1'b0, Qc, Qb, Qa}));  // open: dp

  // Other names for the same wires on the sheet: Kb = Jb; Kc = Jc
endmodule
